// Logisim project control-logic.circ as structural Verilog: 1 circuit, main circuit control_logic
module control_logic (
  input  [31:0] Instruction,
  input  BrEq,
  input  BrLt,
  output PCSel,
  output RegWEn,
  output [2:0] ImmSel,
  output BrUn,
  output ASel,
  output BSel,
  output [3:0] ALUSel,
  output MemWEn,
  output [1:0] WBSel
);

  wire bge, bneq, comparator_1_eq, comparator_2_eq, comparator_3_eq, comparator_4_eq, comparator_8_eq,
       comparator_9_eq, comparator_22_eq, comparator_23_eq, comparator_26_eq, comparator_29_eq,
       comparator_32_eq, comparator_35_eq, comparator_42_eq, comparator_43_eq, is_add, is_addi, is_and,
       is_andi, is_auipc, is_B, is_beq, is_bge, is_bgeu, is_blt, is_bltu, is_bne, is_jal, is_Jal_or_Jalr,
       is_jalr, is_lb, is_lh, is_lui, is_lw, is_mul, is_mulh, is_mulhu, is_or, is_ori, is_sb, is_sh, is_sll,
       is_slli, is_slt, is_slti, is_sra, is_srai, is_srl, is_srli, is_sub, is_sw, is_xor, is_xori, or_1_out,
       PCSel0;
  wire [2:0] bit_extender_2_out, bit_extender_3_out, bit_extender_4_out, bit_extender_5_out, fun3_or0_B,
       fun3_or0_I1, fun3_or0_I2, fun3_or0_S, PCSel_value;
  wire [5:0] ROM_input;
  wire [9:0] bit_extender_1_out, fun3fun7;
  wire [15:14] rom_1_data;

  assign bit_extender_1_out = {{9{comparator_1_eq}}, comparator_1_eq};  // Bit_Extender bit_extender_1
  Comparator #(.width(7)) comparator_1 (.a(7'b0110011), .b(Instruction[6:0]), .eq(comparator_1_eq));  // open: gt, lt
  Comparator #(.width(7)) comparator_2 (.a(7'b0010011), .b(Instruction[6:0]), .eq(comparator_2_eq));  // open: gt, lt
  Comparator #(.width(7)) comparator_3 (.a(7'b0000011), .b(Instruction[6:0]), .eq(comparator_3_eq));  // open: gt, lt
  Comparator #(.width(7)) comparator_4 (.a(7'b0100011), .b(Instruction[6:0]), .eq(comparator_4_eq));  // open: gt, lt
  Comparator #(.width(7)) comparator_5 (.a(7'b1100011), .b(Instruction[6:0]), .eq(is_B));  // open: gt, lt
  assign fun3fun7 = bit_extender_1_out & {Instruction[14:12], Instruction[31:25]};  // AND_Gate and_1, 10 bits wide
  assign bit_extender_2_out = {{2{comparator_2_eq}}, comparator_2_eq};  // Bit_Extender bit_extender_2
  assign bit_extender_3_out = {{2{comparator_3_eq}}, comparator_3_eq};  // Bit_Extender bit_extender_3
  assign bit_extender_4_out = {{2{comparator_4_eq}}, comparator_4_eq};  // Bit_Extender bit_extender_4
  assign bit_extender_5_out = {{2{is_B}}, is_B};  // Bit_Extender bit_extender_5
  Comparator #(.width(7)) comparator_6 (.a(7'b0010111), .b(Instruction[6:0]), .eq(is_auipc));  // open: gt, lt
  Comparator #(.width(7)) comparator_7 (.a(7'b0110111), .b(Instruction[6:0]), .eq(is_lui));  // open: gt, lt
  ROM #(.addrWidth(6), .dataWidth(16)) rom_1 (
    .addr(ROM_input), .data({rom_1_data, WBSel, MemWEn, ALUSel, BSel, ASel, BrUn, ImmSel, RegWEn}));
  assign fun3_or0_I1 = bit_extender_2_out & Instruction[14:12];  // AND_Gate and_2, 3 bits wide
  assign fun3_or0_I2 = bit_extender_3_out & Instruction[14:12];  // AND_Gate and_3, 3 bits wide
  assign fun3_or0_S = bit_extender_4_out & Instruction[14:12];  // AND_Gate and_4, 3 bits wide
  assign fun3_or0_B = bit_extender_5_out & Instruction[14:12];  // AND_Gate and_5, 3 bits wide
  Comparator #(.width(3)) comparator_8 (.a(fun3_or0_I1), .b(3'b101), .eq(comparator_8_eq));  // open: gt, lt
  Comparator #(.width(10)) comparator_9 (.a(fun3fun7), .b({10{1'b0}}), .eq(comparator_9_eq));  // open: gt, lt
  Comparator #(.width(10)) comparator_10 (.a(fun3fun7), .b(10'h1), .eq(is_mul));  // open: gt, lt
  Comparator #(.width(10)) comparator_11 (.a(fun3fun7), .b(10'h20), .eq(is_sub));  // open: gt, lt
  Comparator #(.width(10)) comparator_12 (.a(fun3fun7), .b(10'h80), .eq(is_sll));  // open: gt, lt
  Comparator #(.width(10)) comparator_13 (.a(fun3fun7), .b(10'h81), .eq(is_mulh));  // open: gt, lt
  Comparator #(.width(10)) comparator_14 (.a(fun3fun7), .b(10'h181), .eq(is_mulhu));  // open: gt, lt
  Comparator #(.width(10)) comparator_15 (.a(fun3fun7), .b(10'h100), .eq(is_slt));  // open: gt, lt
  Comparator #(.width(10)) comparator_16 (.a(fun3fun7), .b(10'h200), .eq(is_xor));  // open: gt, lt
  Comparator #(.width(10)) comparator_17 (.a(fun3fun7), .b(10'h280), .eq(is_srl));  // open: gt, lt
  Comparator #(.width(10)) comparator_18 (.a(fun3fun7), .b(10'h2a0), .eq(is_sra));  // open: gt, lt
  Comparator #(.width(10)) comparator_19 (.a(fun3fun7), .b(10'h300), .eq(is_or));  // open: gt, lt
  Comparator #(.width(10)) comparator_20 (.a(fun3fun7), .b(10'h380), .eq(is_and));  // open: gt, lt
  Comparator #(.width(3)) comparator_21 (.a(fun3_or0_I1), .b(3'b100), .eq(is_xori));  // open: gt, lt
  Comparator #(.width(7)) comparator_22 (.a(Instruction[31:25]), .b({7{1'b0}}), .eq(comparator_22_eq));  // open: gt, lt
  Comparator #(.width(7)) comparator_23 (
    .a(Instruction[31:25]), .b(7'b0100000), .eq(comparator_23_eq));  // open: gt, lt
  Comparator #(.width(3)) comparator_24 (.a(fun3_or0_I1), .b(3'b110), .eq(is_ori));  // open: gt, lt
  Comparator #(.width(3)) comparator_25 (.a(fun3_or0_I1), .b(3'b111), .eq(is_andi));  // open: gt, lt
  and and_6 (is_add, comparator_9_eq, comparator_1_eq);
  Comparator #(.width(3)) comparator_26 (.a(fun3_or0_I1), .b(3'b000), .eq(comparator_26_eq));  // open: gt, lt
  Comparator #(.width(3)) comparator_27 (.a(fun3_or0_I1), .b(3'b001), .eq(is_slli));  // open: gt, lt
  Comparator #(.width(3)) comparator_28 (.a(fun3_or0_I1), .b(3'b010), .eq(is_slti));  // open: gt, lt
  and and_7 (is_srli, comparator_8_eq, comparator_22_eq);
  and and_8 (is_srai, comparator_8_eq, comparator_23_eq);
  Comparator #(.width(3)) comparator_29 (.a(fun3_or0_I2), .b(3'b000), .eq(comparator_29_eq));  // open: gt, lt
  Comparator #(.width(3)) comparator_30 (.a(fun3_or0_I2), .b(3'b001), .eq(is_lh));  // open: gt, lt
  Comparator #(.width(3)) comparator_31 (.a(fun3_or0_I2), .b(3'b010), .eq(is_lw));  // open: gt, lt
  Comparator #(.width(3)) comparator_32 (.a(fun3_or0_S), .b(3'b000), .eq(comparator_32_eq));  // open: gt, lt
  Comparator #(.width(3)) comparator_33 (.a(fun3_or0_S), .b(3'b001), .eq(is_sh));  // open: gt, lt
  Comparator #(.width(3)) comparator_34 (.a(fun3_or0_S), .b(3'b010), .eq(is_sw));  // open: gt, lt
  Comparator #(.width(3)) comparator_35 (.a(fun3_or0_B), .b(3'b000), .eq(comparator_35_eq));  // open: gt, lt
  Comparator #(.width(3)) comparator_36 (.a(fun3_or0_B), .b(3'b001), .eq(is_bne));  // open: gt, lt
  Comparator #(.width(3)) comparator_37 (.a(fun3_or0_B), .b(3'b100), .eq(is_blt));  // open: gt, lt
  Comparator #(.width(3)) comparator_38 (.a(fun3_or0_B), .b(3'b101), .eq(is_bge));  // open: gt, lt
  Comparator #(.width(3)) comparator_39 (.a(fun3_or0_B), .b(3'b110), .eq(is_bltu));  // open: gt, lt
  Comparator #(.width(3)) comparator_40 (.a(fun3_or0_B), .b(3'b111), .eq(is_bgeu));  // open: gt, lt
  and and_9 (is_addi, comparator_2_eq, comparator_26_eq);
  and and_10 (is_lb, comparator_3_eq, comparator_29_eq);
  and and_11 (is_sb, comparator_4_eq, comparator_32_eq);
  and and_12 (is_beq, is_B, comparator_35_eq);
  // Priority_Encoder #(.select_enc(6)) priority_encoder_1: pin names not known; wires that end beside it: ROM_input, is_add, is_mul, is_sub, is_sll, is_mulh, is_mulhu, is_slt, is_xor, is_srl, is_sra, is_or, is_and, is_lb, is_lh, is_lw, is_addi, is_slli, is_slti, is_xori, is_srli, is_srai, is_ori, is_andi, is_sb, is_sh, is_sw, is_beq, is_bne, is_blt, is_bge, is_bltu, is_bgeu, is_auipc, is_lui, is_jal, is_jalr
  Comparator #(.width(7)) comparator_41 (.a(7'b1101111), .b(Instruction[6:0]), .eq(is_jal));  // open: gt, lt
  Comparator #(.width(7)) comparator_42 (.a(7'b1100111), .b(Instruction[6:0]), .eq(comparator_42_eq));  // open: gt, lt
  Comparator #(.width(3)) comparator_43 (.a(3'b000), .b(Instruction[14:12]), .eq(comparator_43_eq));  // open: gt, lt
  not not_1 (bneq, BrEq);
  not not_2 (bge, BrLt);
  and and_13 (is_jalr, comparator_42_eq, comparator_43_eq);
  or or_1 (or_1_out, is_jal, is_jalr, is_B);
  or or_2 (is_Jal_or_Jalr, is_jal, is_jalr);
  not not_3 (PCSel0, or_1_out);
  Multiplexer #(.select(3)) multiplexer_1 (
    .in0(BrEq), .in1(bneq), .in2(BrLt), .in3(bge), .in4(BrLt), .in5(BrEq), .in6(1'b0), .in7(1'b1),
    .out(PCSel), .sel(PCSel_value));
  // Priority_Encoder priority_encoder_2: pin names not known; wires that end beside it: PCSel_value, is_beq, is_bne, is_blt, is_bge, is_bltu, is_bgeu, PCSel0, is_Jal_or_Jalr

  // Other names for the same wires on the sheet: fun7[6:0] = Instruction[31:25]; fun3[2:0] = Instruction[14:12];
  //   beq = BrEq; blt = BrLt; Opcode[6:0] = Instruction[6:0]

  // Notes on the sheet:
  //   INPUTS to your circuit
  //   contents of rom_1 (hex, n*v repeats v):
  //   1 401 601 81 481 581 101 201 281 681 301 381 1041 1041 1041 41 c1 141 241 2c1 6c1 341 3c1 842 842
  //   842 4*64 74 74 67 7e7 2069 2041
  //   ROM FOR CONTROL LOGIC
  //   DON'T CHANGE THE LOCATIONS OF THE INPUTS AND OUTPUTS!
  //   This is only if you choose to do the ROM option
  //   CONNECT
  //   WIRE
  //   TO
  //   USE
  //   ROM
  //   OUTPUT from your circuit
  //   Reminder: If using ROM, use combinational logic for PCSel
endmodule
