// Logisim project cpu.circ as structural Verilog: 1 circuit, main circuit cpu
module cpu (
  input  clk,
  input  [31:0] Instruction,
  input  [31:0] MemReadData,
  output [31:0] MemAddress,
  output [31:0] ProgramCounter,
  output [31:0] ra,
  output [31:0] sp,
  output [31:0] t0,
  output [31:0] t1,
  output [31:0] t2,
  output [31:0] s0,
  output [31:0] s1,
  output [31:0] a0,
  output [3:0] MemWriteMask,
  output [31:0] MemWriteData
);

  wire ASel, BrEq, BrLt, BrUn, BSel, MemWEn, PCSel, RegWEn;
  wire [1:0] WBSel;
  wire [2:0] control_logic_1_immsel;
  wire [3:0] ALUSel;
  wire [31:0] dataA, dataB, imm_gen_1_immediate, Instruction_stage2, MemData_result, multiplexer_1_out,
       multiplexer_2_out, PCplus4, rd1_data, rd2_data, register_1_q, register_2_q, WB_result;

  Adder #(.width(32)) adder_1 (.a(ProgramCounter), .b(32'h4), .out(PCplus4));  // open: cin, cout
  Multiplexer #(.width(32)) multiplexer_1 (.in0(PCplus4), .in1(MemAddress), .out(multiplexer_1_out), .sel(PCSel));
  Register #(.width(32)) PC (.D(multiplexer_1_out), .clk(clk), .Q(ProgramCounter));  // open: en, clr
  Register #(.width(32)) imm_register (.D(multiplexer_2_out), .clk(clk), .Q(Instruction_stage2));  // open: en, clr
  Multiplexer #(.width(32)) multiplexer_2 (.in0(Instruction), .in1(32'h13), .out(multiplexer_2_out), .sel(PCSel));
  control_logic control_logic_1 (
    .Instruction(Instruction_stage2), .BrEq(BrEq), .BrLt(BrLt), .PCSel(PCSel), .RegWEn(RegWEn),
    .ImmSel(control_logic_1_immsel), .BrUn(BrUn), .ASel(ASel), .BSel(BSel), .ALUSel(ALUSel), .MemWEn(MemWEn),
    .WBSel(WBSel));
  regfile regfile_1 (
    .ReadIndex1(Instruction_stage2[19:15]), .ReadIndex2(Instruction_stage2[24:20]),
    .WriteIndex(Instruction_stage2[11:7]), .WriteData(WB_result), .RegWEn(RegWEn), .clk(clk), .ra(ra),
    .sp(sp), .t0(t0), .t1(t1), .t2(t2), .s0(s0), .s1(s1), .a0(a0), .ReadData1(rd1_data), .ReadData2(rd2_data));
  imm_gen imm_gen_1 (
    .Instruction(Instruction_stage2), .ImmSel(control_logic_1_immsel), .Immediate(imm_gen_1_immediate));
  Multiplexer #(.width(32)) multiplexer_3 (.in0(rd2_data), .in1(imm_gen_1_immediate), .out(dataB), .sel(BSel));
  Multiplexer #(.width(32)) multiplexer_4 (.in0(rd1_data), .in1(register_1_q), .out(dataA), .sel(ASel));
  Register #(.width(32)) register_1 (.D(ProgramCounter), .clk(clk), .Q(register_1_q));  // open: en, clr
  alu alu_1 (.A(dataA), .B(dataB), .ALUSel(ALUSel), .ALUResult(MemAddress));
  branch_comp branch_comp_1 (.BrData1(rd1_data), .BrData2(rd2_data), .BrUn(BrUn), .BrEq(BrEq), .BrLt(BrLt));
  Register #(.width(32)) register_2 (.D(PCplus4), .clk(clk), .Q(register_2_q));  // open: en, clr
  partial_store partial_store_1 (
    .Instruction(Instruction_stage2), .MemAddress(MemAddress), .DataFromReg(rd2_data), .MemWEn(MemWEn),
    .MemWriteMask(MemWriteMask), .DataToMem(MemWriteData));
  partial_load partial_load_1 (
    .Instruction(Instruction_stage2), .MemAddress(MemAddress), .DataFromMem(MemReadData),
    .DataToReg(MemData_result));
  Multiplexer #(.select(2), .width(32)) multiplexer_5 (
    .in0(MemAddress), .in1(MemData_result), .in2(register_2_q), .out(WB_result), .sel(WBSel));  // open: in3

  // Other names for the same wires on the sheet: ALU_result[31:0] = MemAddress

  // Notes on the sheet:
  //   To IMEM
  //   IMEM (do **NOT** move this)
  //   From IMEM
  //   Inputs/Outputs for testing. Do **NOT** move these.
  //   It is OK to move the PC, RegFile, ALU, MEM, Branch Comp, Imm Gen, Partial Load, Partial Store and Control Logic to wherever is most convenient for you when constructing your CPU, and to delete this text
  //   To DMEM
  //   DMEM (do **NOT** move this)
  //   From DMEM
endmodule
