// Logisim project partial-load.circ as structural Verilog: 1 circuit, main circuit partial_load
module partial_load (
  input  [31:0] Instruction,
  input  [31:0] MemAddress,
  input  [31:0] DataFromMem,
  output [31:0] DataToReg
);

  wire comparator_1_eq, comparator_2_eq, is_index_0, is_index_1, is_index_2, is_index_3, is_lb, is_lh, is_lw;
  wire [1:0] sel_instru, sel_startBit;
  wire [2:0] bit_extender_8_out, funct3_or0;
  wire [31:0] bit_extender_1_out, bit_extender_2_out, bit_extender_3_out, bit_extender_4_out,
       bit_extender_5_out, bit_extender_6_out, bit_extender_7_out, DataOutputLoadByte, DataOutputLoadHalf;

  // Priority_Encoder #(.select_enc(2)) priority_encoder_1: pin names not known; wires that end beside it: sel_instru, is_lb, is_lh, is_lw
  // Priority_Encoder #(.select_enc(2)) priority_encoder_2: pin names not known; wires that end beside it: sel_startBit, DataFromMem[7:0], is_index_0, is_index_1, is_index_2, is_index_3
  Comparator #(.width(7)) comparator_1 (.a(7'b0000011), .b(Instruction[6:0]), .eq(comparator_1_eq));  // open: gt, lt
  Comparator #(.width(3)) comparator_2 (.a(funct3_or0), .b(3'b000), .eq(comparator_2_eq));  // open: gt, lt
  Comparator #(.width(3)) comparator_3 (.a(funct3_or0), .b(3'b001), .eq(is_lh));  // open: gt, lt
  Comparator #(.width(3)) comparator_4 (.a(funct3_or0), .b(3'b010), .eq(is_lw));  // open: gt, lt
  Comparator #(.width(2)) comparator_5 (.a(MemAddress[1:0]), .b(2'b00), .eq(is_index_0));  // open: gt, lt
  Comparator #(.width(2)) comparator_6 (.a(MemAddress[1:0]), .b(2'b01), .eq(is_index_1));  // open: gt, lt
  Comparator #(.width(2)) comparator_7 (.a(MemAddress[1:0]), .b(2'b10), .eq(is_index_2));  // open: gt, lt
  Comparator #(.width(2)) comparator_8 (.a(MemAddress[1:0]), .b(2'b11), .eq(is_index_3));  // open: gt, lt
  assign bit_extender_1_out = {{24{DataFromMem[7]}}, DataFromMem[7:0]};  // Bit_Extender bit_extender_1
  assign bit_extender_2_out = {{24{DataFromMem[15]}}, DataFromMem[15:8]};  // Bit_Extender bit_extender_2
  assign bit_extender_3_out = {{24{DataFromMem[23]}}, DataFromMem[23:16]};  // Bit_Extender bit_extender_3
  assign bit_extender_4_out = {{24{DataFromMem[31]}}, DataFromMem[31:24]};  // Bit_Extender bit_extender_4
  assign bit_extender_5_out = {{16{DataFromMem[15]}}, DataFromMem[15:0]};  // Bit_Extender bit_extender_5
  assign bit_extender_6_out = {{16{DataFromMem[23]}}, DataFromMem[23:8]};  // Bit_Extender bit_extender_6
  assign bit_extender_7_out = {{16{DataFromMem[31]}}, DataFromMem[31:16]};  // Bit_Extender bit_extender_7
  assign bit_extender_8_out = {{2{comparator_1_eq}}, comparator_1_eq};  // Bit_Extender bit_extender_8
  and and_1 (is_lb, comparator_2_eq, comparator_1_eq);
  Multiplexer #(.select(2), .width(32)) multiplexer_1 (
    .in0(bit_extender_5_out), .in1(bit_extender_6_out), .in2(bit_extender_7_out), .out(DataOutputLoadHalf),
    .sel(sel_startBit));  // open: in3
  assign funct3_or0 = bit_extender_8_out & Instruction[14:12];  // AND_Gate and_2, 3 bits wide
  Multiplexer #(.select(2), .width(32)) multiplexer_2 (
    .in0(bit_extender_1_out), .in1(bit_extender_2_out), .in2(bit_extender_3_out), .in3(bit_extender_4_out),
    .out(DataOutputLoadByte), .sel(sel_startBit));
  Multiplexer #(.select(2), .width(32)) multiplexer_3 (
    .in0(DataOutputLoadByte), .in1(DataOutputLoadHalf), .in2(DataFromMem), .out(DataToReg), .sel(sel_instru));  // open: in3

  // Other names for the same wires on the sheet: Opcode[6:0] = Instruction[6:0]; funct3[2:0] = Instruction[14:12];
  //   last2bits_memAddr[1:0] = MemAddress[1:0]

  // Notes on the sheet:
  //   INPUTS to your circuit
  //   DON'T CHANGE THE LOCATIONS OF THE INPUTS AND OUTPUTS!
  //   OUTPUT from your circuit
endmodule
