// Logisim project partial-store.circ as structural Verilog: 1 circuit, main circuit partial_store
module partial_store (
  input  [31:0] Instruction,
  input  [31:0] MemAddress,
  input  [31:0] DataFromReg,
  input  MemWEn,
  output [3:0] MemWriteMask,
  output [31:0] DataToMem
);

  wire comparator_8_eq, comparator_9_eq, comparator_10_eq, demultiplexer_1_out0, demultiplexer_1_out1,
       demultiplexer_1_out2, demultiplexer_1_out3, is_index_0, is_index_1, is_index_2, is_index_3, is_not,
       is_sb, is_sb_0, is_sb_1, is_sb_2, is_sb_3, is_sh, is_sh_0, is_sh_1, is_sh_2, is_sw, or_1_out,
       priority_encoder_1_p6, priority_encoder_3_p2;
  wire [1:0] sel_instru, sel_startBit;
  wire [2:0] bit_extender_8_out, funct3_or0;
  wire [31:0] bit_extender_1_out, bit_extender_2_out, bit_extender_3_out, bit_extender_4_out,
       bit_extender_5_out, bit_extender_6_out, bit_extender_7_out, sb_output, sh_output, shifter_1_out,
       shifter_2_out, shifter_3_out, shifter_4_out, shifter_5_out;

  assign bit_extender_1_out = {{24{1'b0}}, DataFromReg[7:0]};  // Bit_Extender bit_extender_1
  assign bit_extender_2_out = {{24{1'b0}}, DataFromReg[7:0]};  // Bit_Extender bit_extender_2
  assign bit_extender_3_out = {{24{1'b0}}, DataFromReg[7:0]};  // Bit_Extender bit_extender_3
  // Priority_Encoder #(.select_enc(2)) priority_encoder_1: pin names not known; wires that end beside it: sel_instru, is_sb, is_sh, is_sw, is_not, priority_encoder_1_p6
  // Priority_Encoder #(.select_enc(2)) priority_encoder_2: pin names not known; wires that end beside it: sel_startBit, is_index_0, is_index_1, is_index_2, is_index_3
  assign bit_extender_4_out = {{24{1'b0}}, DataFromReg[7:0]};  // Bit_Extender bit_extender_4
  Shifter #(.width(32)) shifter_1 (.in(bit_extender_1_out), .\dist (5'b01000), .out(shifter_1_out));
  Shifter #(.width(32)) shifter_2 (.in(bit_extender_2_out), .\dist (5'b10000), .out(shifter_2_out));
  Shifter #(.width(32)) shifter_3 (.in(bit_extender_3_out), .\dist (5'b11000), .out(shifter_3_out));
  assign bit_extender_5_out = {{16{1'b0}}, DataFromReg[15:0]};  // Bit_Extender bit_extender_5
  assign bit_extender_6_out = {{16{1'b0}}, DataFromReg[15:0]};  // Bit_Extender bit_extender_6
  assign bit_extender_7_out = {{16{1'b0}}, DataFromReg[15:0]};  // Bit_Extender bit_extender_7
  Comparator #(.width(3)) comparator_1 (.a(funct3_or0), .b(3'b001), .eq(is_sh));  // open: gt, lt
  Comparator #(.width(3)) comparator_2 (.a(funct3_or0), .b(3'b010), .eq(is_sw));  // open: gt, lt
  Comparator #(.width(2)) comparator_3 (.a(MemAddress[1:0]), .b(2'b00), .eq(is_index_0));  // open: gt, lt
  Comparator #(.width(2)) comparator_4 (.a(MemAddress[1:0]), .b(2'b01), .eq(is_index_1));  // open: gt, lt
  Comparator #(.width(2)) comparator_5 (.a(MemAddress[1:0]), .b(2'b10), .eq(is_index_2));  // open: gt, lt
  Comparator #(.width(2)) comparator_6 (.a(MemAddress[1:0]), .b(2'b11), .eq(is_index_3));  // open: gt, lt
  Shifter #(.width(32)) shifter_4 (.in(bit_extender_6_out), .\dist (5'b01000), .out(shifter_4_out));
  Shifter #(.width(32)) shifter_5 (.in(bit_extender_7_out), .\dist (5'b10000), .out(shifter_5_out));
  assign bit_extender_8_out = {{2{priority_encoder_1_p6}}, priority_encoder_1_p6};  // Bit_Extender bit_extender_8
  Comparator #(.width(7)) comparator_7 (
    .a(7'b0100011), .b(Instruction[6:0]), .eq(priority_encoder_1_p6));  // open: gt, lt
  Comparator #(.width(3)) comparator_8 (.a(funct3_or0), .b(3'b000), .eq(comparator_8_eq));  // open: gt, lt
  Multiplexer #(.select(2), .width(32)) multiplexer_1 (
    .in0(bit_extender_4_out), .in1(shifter_1_out), .in2(shifter_2_out), .in3(shifter_3_out), .out(sb_output),
    .sel(sel_startBit));
  Multiplexer #(.select(2), .width(32)) multiplexer_2 (
    .in0(bit_extender_5_out), .in1(shifter_4_out), .in2(shifter_5_out), .out(sh_output), .sel(sel_startBit));  // open: in3
  assign funct3_or0 = bit_extender_8_out & Instruction[14:12];  // AND_Gate and_1, 3 bits wide
  and and_2 (is_sb, comparator_8_eq, priority_encoder_1_p6);
  or or_1 (or_1_out, is_sw, is_sb, is_sh);
  not not_1 (is_not, or_1_out);
  Demultiplexer #(.select(2)) demultiplexer_1 (
    .out0(demultiplexer_1_out0), .out1(demultiplexer_1_out1), .out2(demultiplexer_1_out2),
    .out3(demultiplexer_1_out3), .in(1'b1), .sel(sel_startBit));
  Comparator #(.width(2)) comparator_9 (.a(sel_instru), .b(2'b00), .eq(comparator_9_eq));  // open: gt, lt
  Comparator #(.width(2)) comparator_10 (.a(sel_instru), .b(2'b01), .eq(comparator_10_eq));  // open: gt, lt
  Comparator #(.width(2)) comparator_11 (.a(sel_instru), .b(2'b10), .eq(is_sw));  // open: gt, lt
  Multiplexer #(.select(2), .width(32)) multiplexer_3 (
    .in0(sb_output), .in1(sh_output), .in2(DataFromReg), .in3({32{1'b0}}), .out(DataToMem), .sel(sel_instru));
  and and_3 (is_sb_0, comparator_9_eq, demultiplexer_1_out0);
  and and_4 (is_sb_1, demultiplexer_1_out1, comparator_9_eq);
  and and_5 (is_sb_2, comparator_9_eq, demultiplexer_1_out2);
  and and_6 (is_sb_3, comparator_9_eq, demultiplexer_1_out3);
  and and_7 (is_sh_0, comparator_10_eq, demultiplexer_1_out0);
  and and_8 (is_sh_1, comparator_10_eq, demultiplexer_1_out1);
  and and_9 (is_sh_2, demultiplexer_1_out2, comparator_10_eq);
  // Priority_Encoder #(.select_enc(4)) priority_encoder_3: pin names not known; wires that end beside it: MemWriteMask, priority_encoder_3_p2, is_sb_0, is_sb_1, is_sh_0, is_sb_2, is_sh_1, is_sb_3, is_sh_2, is_sw
  not not_2 (priority_encoder_3_p2, MemWEn);

  // Other names for the same wires on the sheet: least2_byte[15:0] = DataFromReg[15:0];
  //   least_byte[7:0] = DataFromReg[7:0]; Opcode[6:0] = Instruction[6:0]; funct3[2:0] = Instruction[14:12];
  //   last2bits_memAddr[1:0] = MemAddress[1:0]

  // Notes on the sheet:
  //   INPUTS to your circuit
  //   DON'T CHANGE THE LOCATIONS OF THE INPUTS AND OUTPUTS!
  //   OUTPUT from your circuit
endmodule
