// Logisim project regfile.circ as structural Verilog: 1 circuit, main circuit regfile
module regfile (
  input  [4:0] ReadIndex1,
  input  [4:0] ReadIndex2,
  input  [4:0] WriteIndex,
  input  [31:0] WriteData,
  input  RegWEn,
  input  clk,
  output [31:0] ra,
  output [31:0] sp,
  output [31:0] t0,
  output [31:0] t1,
  output [31:0] t2,
  output [31:0] s0,
  output [31:0] s1,
  output [31:0] a0,
  output [31:0] ReadData1,
  output [31:0] ReadData2
);

  wire m1, m2, m3, m4, m5, m6, m7, m8, m9, m10, m11, m12, m13, m14, m15, m16, m17, m18, m19, m20, m21, m23,
       m24, m25, m26, m27, m28, m29, m30, m31, undriven;
  wire [31:0] demultiplexer_2_out0, x0, x1, x1D, x2, x2D, x3, x3D, x3Q, x4, x4D, x4Q, x5, x5D, x6, x6D, x7,
       x7D, x8, x8D, x9, x9D, x10, x10D, x11, x11D, x11Q, x12, x12D, x12Q, x13, x13D, x13Q, x14, x14D, x14Q,
       x15, x15D, x15Q, x16, x16D, x16Q, x17, x17D, x17Q, x18, x18D, x18Q, x19, x19D, x19Q, x20, x20D, x20Q,
       x21, x21D, x21Q, x22, x22D, x22Q, x23, x23D, x23Q, x24, x24D, x24Q, x25, x25D, x25Q, x26, x26D, x26Q,
       x27, x27D, x27Q, x28, x28D, x28Q, x29, x29D, x29Q, x30, x30D, x30Q, x31, x31D, x31Q;

  Demultiplexer #(.select(5)) demultiplexer_1 (
    .out1(m1), .out2(m2), .out3(m3), .out4(m4), .out5(m5), .out6(m6), .out7(m7), .out8(m8), .out9(m9),
    .out10(m10), .out11(m11), .out12(m12), .out13(m13), .out14(m14), .out15(m15), .out16(m16), .out17(m17),
    .out18(m18), .out19(m19), .out20(m20), .out21(m21), .out22(m21), .out23(m23), .out24(m24), .out25(m25),
    .out26(m26), .out27(m27), .out28(m28), .out29(m29), .out30(m30), .out31(m31), .in(1'b1), .sel(WriteIndex));  // open: out0
  Demultiplexer #(.select(5), .width(32)) demultiplexer_2 (
    .out0(demultiplexer_2_out0), .out1(x1), .out2(x2), .out3(x3), .out4(x4), .out5(x5), .out6(x6), .out7(x7),
    .out8(x8), .out9(x9), .out10(x10), .out11(x11), .out12(x12), .out13(x13), .out14(x14), .out15(x15),
    .out16(x16), .out17(x17), .out18(x18), .out19(x19), .out20(x20), .out21(x21), .out22(x22), .out23(x23),
    .out24(x24), .out25(x25), .out26(x26), .out27(x27), .out28(x28), .out29(x29), .out30(x30), .out31(x31),
    .in(WriteData), .sel(WriteIndex));
  Register #(.width(32)) u_x28 (.D(x28D), .en(RegWEn), .clk(clk), .Q(x28Q));  // open: clr
  Register #(.width(32)) u_x29 (.D(x29D), .en(RegWEn), .clk(clk), .Q(x29Q));  // open: clr
  Register #(.width(32)) u_x30 (.D(x30D), .en(RegWEn), .clk(clk), .Q(x30Q));  // open: clr
  Register #(.width(32)) u_x31 (.D(x31D), .en(RegWEn), .clk(clk), .Q(x31Q));  // open: clr
  Register #(.width(32)) register_1 (.D({32{1'b0}}), .Q(x0), .clr(clk));  // open: en, clk
  Register #(.width(32)) u_x16 (.D(x16D), .en(RegWEn), .clk(clk), .Q(x16Q));  // open: clr
  Register #(.width(32)) u_x17 (.D(x17D), .en(RegWEn), .clk(clk), .Q(x17Q));  // open: clr
  Register #(.width(32)) u_x18 (.D(x18D), .en(RegWEn), .clk(clk), .Q(x18Q));  // open: clr
  Register #(.width(32)) u_x19 (.D(x19D), .en(RegWEn), .clk(clk), .Q(x19Q));  // open: clr
  Register #(.width(32)) u_x20 (.D(x20D), .en(RegWEn), .clk(clk), .Q(x20Q));  // open: clr
  Register #(.width(32)) u_x21 (.D(x21D), .en(RegWEn), .clk(clk), .Q(x21Q));  // open: clr
  Register #(.width(32)) u_x22 (.D(x22D), .en(RegWEn), .clk(clk), .Q(x22Q));  // open: clr
  Register #(.width(32)) u_x23 (.D(x23D), .en(RegWEn), .clk(clk), .Q(x23Q));  // open: clr
  Register #(.width(32)) u_x24 (.D(x24D), .en(RegWEn), .clk(clk), .Q(x24Q));  // open: clr
  Register #(.width(32)) u_x25 (.D(x25D), .en(RegWEn), .clk(clk), .Q(x25Q));  // open: clr
  Register #(.width(32)) u_x26 (.D(x26D), .en(RegWEn), .clk(clk), .Q(x26Q));  // open: clr
  Register #(.width(32)) u_x27 (.D(x27D), .en(RegWEn), .clk(clk), .Q(x27Q));  // open: clr
  Register #(.width(32)) u_x1 (.D(x1D), .en(RegWEn), .clk(clk), .Q(ra));  // open: clr
  Register #(.width(32)) u_x2 (.D(x2D), .en(RegWEn), .clk(clk), .Q(sp));  // open: clr
  Register #(.width(32)) u_x5 (.D(x5D), .en(RegWEn), .clk(clk), .Q(t0));  // open: clr
  Register #(.width(32)) u_x6 (.D(x6D), .en(RegWEn), .clk(clk), .Q(t1), .clr(undriven));
  Register #(.width(32)) u_x7 (.D(x7D), .en(RegWEn), .clk(clk), .Q(t2));  // open: clr
  Register #(.width(32)) u_x8 (.D(x8D), .en(RegWEn), .clk(clk), .Q(s0));  // open: clr
  Register #(.width(32)) u_x9 (.D(x9D), .en(RegWEn), .clk(clk), .Q(s1));  // open: clr
  Register #(.width(32)) u_x10 (.D(x10D), .en(RegWEn), .clk(clk), .Q(a0));  // open: clr
  Register #(.width(32)) u_x3 (.D(x3D), .en(RegWEn), .clk(clk), .Q(x3Q));  // open: clr
  Register #(.width(32)) u_x4 (.D(x4D), .en(RegWEn), .clk(clk), .Q(x4Q));  // open: clr
  Register #(.width(32)) u_x11 (.D(x11D), .en(RegWEn), .clk(clk), .Q(x11Q));  // open: clr
  Register #(.width(32)) u_x12 (.D(x12D), .en(RegWEn), .clk(clk), .Q(x12Q));  // open: clr
  Register #(.width(32)) u_x13 (.D(x13D), .en(RegWEn), .clk(clk), .Q(x13Q));  // open: clr
  Register #(.width(32)) u_x14 (.D(x14D), .en(RegWEn), .clk(clk), .Q(x14Q));  // open: clr
  Register #(.width(32)) u_x15 (.D(x15D), .en(RegWEn), .clk(clk), .Q(x15Q));  // open: clr
  Multiplexer #(.select(5), .width(32)) multiplexer_1 (
    .in0(x0), .in1(ra), .in2(sp), .in3(x3Q), .in4(x4Q), .in5(t0), .in6(t1), .in7(t2), .in8(s0), .in9(s1),
    .in10(a0), .in11(x11Q), .in12(x12Q), .in13(x13Q), .in14(x14Q), .in15(x15Q), .in16(x16Q), .in17(x17Q),
    .in18(x18Q), .in19(x19Q), .in20(x20Q), .in21(x21Q), .in22(x22Q), .in23(x23Q), .in24(x24Q), .in25(x25Q),
    .in26(x26Q), .in27(x27Q), .in28(x28Q), .in29(x29Q), .in30(x30Q), .in31(x31Q), .out(ReadData1),
    .sel(ReadIndex1));
  Multiplexer #(.select(5), .width(32)) multiplexer_2 (
    .in0(x0), .in1(ra), .in2(sp), .in3(x3Q), .in4(x4Q), .in5(t0), .in6(t1), .in7(t2), .in8(s0), .in9(s1),
    .in10(a0), .in11(x11Q), .in12(x12Q), .in13(x13Q), .in14(x14Q), .in15(x15Q), .in16(x16Q), .in17(x17Q),
    .in18(x18Q), .in19(x19Q), .in20(x20Q), .in21(x21Q), .in22(x22Q), .in23(x23Q), .in24(x24Q), .in25(x25Q),
    .in26(x26Q), .in27(x27Q), .in28(x28Q), .in29(x29Q), .in30(x30Q), .in31(x31Q), .out(ReadData2),
    .sel(ReadIndex2));
  Multiplexer #(.width(32)) multiplexer_3 (.in0(s0), .in1(x8), .out(x8D), .sel(m8));
  Multiplexer #(.width(32)) multiplexer_4 (.in0(a0), .in1(x10), .out(x10D), .sel(m10));
  Multiplexer #(.width(32)) multiplexer_5 (.in0(x11Q), .in1(x11), .out(x11D), .sel(m11));
  Multiplexer #(.width(32)) multiplexer_6 (.in0(x12Q), .in1(x12), .out(x12D), .sel(m12));
  Multiplexer #(.width(32)) multiplexer_7 (.in0(x13Q), .in1(x13), .out(x13D), .sel(m13));
  Multiplexer #(.width(32)) multiplexer_8 (.in0(x14Q), .in1(x14), .out(x14D), .sel(m14));
  Multiplexer #(.width(32)) multiplexer_9 (.in0(x15Q), .in1(x15), .out(x15D), .sel(m15));
  Multiplexer #(.width(32)) multiplexer_10 (.in0(x16Q), .in1(x16), .out(x16D), .sel(m16));
  Multiplexer #(.width(32)) multiplexer_11 (.in0(ra), .in1(x1), .out(x1D), .sel(m1));
  Multiplexer #(.width(32)) multiplexer_12 (.in0(sp), .in1(x2), .out(x2D), .sel(m2));
  Multiplexer #(.width(32)) multiplexer_13 (.in0(x3Q), .in1(x3), .out(x3D), .sel(m3));
  Multiplexer #(.width(32)) multiplexer_14 (.in0(x4Q), .in1(x4), .out(x4D), .sel(m4));
  Multiplexer #(.width(32)) multiplexer_15 (.in0(t0), .in1(x5), .out(x5D), .sel(m5));
  Multiplexer #(.width(32)) multiplexer_16 (.in0(t1), .in1(x6), .out(x6D), .sel(m6));
  Multiplexer #(.width(32)) multiplexer_17 (.in0(t2), .in1(x7), .out(x7D), .sel(m7));
  Multiplexer #(.width(32)) multiplexer_18 (.in0(s1), .in1(x9), .out(x9D), .sel(m9));
  Multiplexer #(.width(32)) multiplexer_19 (.in0(x24Q), .in1(x24), .out(x24D), .sel(m24));
  Multiplexer #(.width(32)) multiplexer_20 (.in0(x17Q), .in1(x17), .out(x17D), .sel(m17));
  Multiplexer #(.width(32)) multiplexer_21 (.in0(x18Q), .in1(x18), .out(x18D), .sel(m18));
  Multiplexer #(.width(32)) multiplexer_22 (.in0(x19Q), .in1(x19), .out(x19D), .sel(m19));
  Multiplexer #(.width(32)) multiplexer_23 (.in0(x20Q), .in1(x20), .out(x20D), .sel(m20));
  Multiplexer #(.width(32)) multiplexer_24 (.in0(x21Q), .in1(x21), .out(x21D), .sel(m21));
  Multiplexer #(.width(32)) multiplexer_25 (.in0(x22Q), .in1(x22), .out(x22D), .sel(m21));
  Multiplexer #(.width(32)) multiplexer_26 (.in0(x23Q), .in1(x23), .out(x23D), .sel(m23));
  Multiplexer #(.width(32)) multiplexer_27 (.in0(x25Q), .in1(x25), .out(x25D), .sel(m25));
  Multiplexer #(.width(32)) multiplexer_28 (.in0(x26Q), .in1(x26), .out(x26D), .sel(m26));
  Multiplexer #(.width(32)) multiplexer_29 (.in0(x27Q), .in1(x27), .out(x27D), .sel(m27));
  Multiplexer #(.width(32)) multiplexer_30 (.in0(x28Q), .in1(x28), .out(x28D), .sel(m28));
  Multiplexer #(.width(32)) multiplexer_31 (.in0(x29Q), .in1(x29), .out(x29D), .sel(m29));
  Multiplexer #(.width(32)) multiplexer_32 (.in0(x30Q), .in1(x30), .out(x30D), .sel(m30));
  Multiplexer #(.width(32)) multiplexer_33 (.in0(x31Q), .in1(x31), .out(x31D), .sel(m31));

  // Other names for the same wires on the sheet: m22 = m21; x1Q[31:0] = ra; x2Q[31:0] = sp; x5Q[31:0] = t0;
  //   x6Q[31:0] = t1; x7Q[31:0] = t2; x8Q[31:0] = s0; x9Q[31:0] = s1; x10Q[31:0] = a0

  // Notes on the sheet:
  //   INPUTS to your circuit
  //   DON'T CHANGE THE LOCATIONS OF THE INPUTS AND OUTPUTS!
  //   These are DEBUG/TEST outputs from your circuit.
  //   OUTPUTS from your circuit
endmodule
